# Fritzing sketch Adder (saved by Fritzing 0.9.3b)
breadboards: 1

parts:
  IC1 = 74HC08 Logic AND Gate [part_number=74HC08 package="DIP (Dual Inline) [THT]"]
  IC2 = 74HC08 Logic AND Gate [part_number=74HC08 package="DIP (Dual Inline) [THT]"]
  SW1 = DIP Switch 8 Position [package=dipswitch-08]
  IC3 = 74HC08 Logic AND Gate [part_number=74HC08 package="DIP (Dual Inline) [THT]"]
  LED1 = LED - 3mm [color="Green (555nm)" package="3 mm [THT]"]
  LED2 = LED - 3mm [color="Green (555nm)" package="3 mm [THT]"]
  R1 = Resistor [tolerance=±5% resistance=1k package="0805 [SMD]"]
  R2 = Resistor [tolerance=±5% resistance=10k package="2010 [SMD]"]
  R3 = Resistor [tolerance=±5% resistance=10k package="2010 [SMD]"]
  R4 = Resistor [tolerance=±5% resistance=10k package="2010 [SMD]"]
  R5 = Resistor [tolerance=±5% resistance=10k package="2010 [SMD]"]
  R6 = Resistor [tolerance=±5% resistance=10k package="2010 [SMD]"]
  R1_2 = Resistor [tolerance=±5% resistance=10k package="2512 [SMD]"]

nets:
  GND: IC1.GND, IC2.GND, IC3.GND, LED1.anode, LED2.anode, R1.Pin_1, R2.Pin_1, R3.Pin_1, R4.Pin_1, R5.Pin_1, R6.Pin_1, R1_2.Pin_1
  N1: IC1.3Y, LED1.cathode
  N2: IC1.3A, IC2.2A, SW1.8, R3.Pin_0
  N3: IC1.3B, IC1.4Y, IC2.2B, R4.Pin_0
  N4: IC1.4A, IC1.4B, IC2.1A, IC2.1B, SW1.1, R1.Pin_0, R2.Pin_0, R1_2.Pin_0
  VCC: IC1.VCC, IC2.VCC, SW1.9, SW1.15, SW1.16, IC3.VCC
  N5: IC2.1Y, IC3.1B, R6.Pin_0
  N6: IC2.2Y, IC3.1A, R5.Pin_0
  N7: IC3.1Y, LED2.cathode
